# Fritzing sketch text_entry_fritzing_schematic (saved by Fritzing 0.9.3b)
breadboards: 2

parts:
  Part1 = RedBear-Duo
  S1 = Pushbutton [package="[THT]"]
  S2 = Pushbutton [package="[THT]"]
  S3 = Pushbutton [package="[THT]"]
  S4 = Pushbutton [package="[THT]"]
  S5 = Pushbutton [package="[THT]"]
  S6 = Pushbutton [package="[THT]"]
  S7 = Pushbutton [package="[THT]"]
  S8 = Pushbutton [package="[THT]"]
  S9 = Pushbutton [package="[THT]"]

nets:
  N1: Part1.A2, S4.Pin_1, S4.Pin_2
  N2: Part1.A4, S3.Pin_1, S3.Pin_2
  N3: Part1.DAC, S2.Pin_1, S2.Pin_2
  N4: Part1.RX, S1.Pin_1, S1.Pin_2
  N5: Part1.GND, S1.Pin_3, S1.Pin_4, S2.Pin_3, S2.Pin_4, S3.Pin_3, S3.Pin_4, S4.Pin_3, S4.Pin_4, S6.Pin_3, S6.Pin_4, S7.Pin_3, S7.Pin_4, S8.Pin_3, S8.Pin_4, S9.Pin_3, S9.Pin_4
  N6: Part1.D0, S9.Pin_1, S9.Pin_2
  N7: Part1.D1, S8.Pin_1, S8.Pin_2
  N8: Part1.D2, S6.Pin_1, S6.Pin_2
  N9: Part1.D4, S7.Pin_1, S7.Pin_2
  N10: Part1.D6, S5.Pin_1, S5.Pin_2
  N11: S5.Pin_3, S5.Pin_4

custom parts:
  RedBear-Duo: Duo is a thumb-size development board made to simplify the building process of Internet of Things (IoT). This part is a modification of the Particle Photon part by Brett Walach,Fabian Althaus
